# Fritzing sketch thruster_schematic (saved by Fritzing 0.9.3b)

parts:
  Jetson_Nano3 = Jetson Nano  # not connected
  Part1 = Arduino Mega ADK (Rev3)
  VCC2 = Battery
  VCC1 = Battery
  Reg1 = DC-DC CONVERTER [part_number=80633 package=dc-dc_converter]
  M2 = ESC
  920KV_Motor2 = DJI 920 KV Motor  # not connected
  920KV_Motor3 = DJI 920 KV Motor  # not connected
  920KV_Motor4 = DJI 920 KV Motor  # not connected
  920KV_Motor5 = DJI 920 KV Motor  # not connected
  920KV_Motor6 = DJI 920 KV Motor  # not connected
  920KV_Motor7 = DJI 920 KV Motor  # not connected
  920KV_Motor8 = DJI 920 KV Motor

nets:
  N1: Part1.D13_PWM, M2.DATA
  5V: Part1.5V, M2.5V
  N2: VCC2.+, VCC1.+, Reg1.IN+
  N3: VCC1.-, Reg1.IN-
  N4: M2.U, 920KV_Motor8.u
  N5: M2.V, 920KV_Motor8.v
  N6: M2.W, 920KV_Motor8.w

custom parts:
  DC-DC CONVERTER: WYHP 5A constant current/voltage manufactured by Shenzhen Weiyapuhua Technology Co., Ltd
  DJI 920 KV Motor: DJI Brushless Outrunner 2212/920K Motor F330-550
